// Logisim project FullSubtractor.circ as structural Verilog: 1 circuit, main circuit main
module main (
  input  X,
  input  Y,
  input  Bin,
  output D,
  output B
);

  wire and_1_out, and_2_out, not_1_out, xor_1_out;

  not not_1 (not_1_out, X);
  xor xor_1 (xor_1_out, Y, Bin);
  and and_1 (and_1_out, Y, Bin);
  xor xor_2 (D, X, xor_1_out);
  and and_2 (and_2_out, not_1_out, xor_1_out);
  or or_1 (B, and_2_out, and_1_out);
endmodule
