// Logisim project HalfSubtractor.circ as structural Verilog: 1 circuit, main circuit main
module main (
  input  Cin,
  input  Y,
  input  X,
  output Sum,
  output out_5
);

  wire and_1_out, and_2_out, xor_1_out;

  xor xor_1 (xor_1_out, Y, X);
  and and_1 (and_1_out, Y, X);
  and and_2 (and_2_out, Cin, xor_1_out);
  xor xor_2 (Sum, Cin, xor_1_out);
  or or_1 (out_5, and_2_out, and_1_out);
endmodule
